// Logisim project Alfabeto NAND e NOR.circ as structural Verilog: 1 circuit, main circuit main
module main (
  input  A,
  input  B,
  input  C,
  input  D,
  input  E,
  input  F
);

  wire nand_1_out, nand_2_out, nand_3_out, nand_4_out, nand_5_out, nand_6_out, nand_7_out, nand_8_out,
       nand_9_out, nand_10_out, nand_11_out, nand_12_out, nand_13_out, nand_14_out, nand_15_out, nand_16_out,
       nand_17_out, nand_18_out, nand_19_out, nand_20_out, nand_21_out, nand_22_out, nand_23_out,
       nand_24_out, nand_25_out, nand_26_out, nand_27_out, nand_28_out, nand_29_out, nand_30_out,
       nand_31_out, nand_32_out, nand_33_out, nand_34_out, nand_35_out, nand_36_out, nand_37_out,
       nand_38_out, nand_39_out, nand_40_out, nand_41_out, nand_42_out, nand_43_out, nand_44_out,
       nand_45_out, nand_46_out, nand_47_out, nand_48_out, nand_49_out, nand_50_out, nand_51_out,
       nand_52_out, nor_1_out, nor_2_out, nor_3_out, nor_4_out, nor_5_out, nor_6_out, nor_7_out, nor_8_out,
       nor_9_out, nor_10_out, nor_11_out, nor_12_out, nor_13_out, nor_14_out, nor_15_out, nor_16_out,
       nor_17_out, nor_18_out, nor_19_out;

  nand nand_1 (nand_1_out, C, D, E);
  nand nand_2 (nand_2_out, B, ~D, F);  // NAND_Gate
  nand nand_3 (nand_3_out, A, ~E, ~F);  // NAND_Gate
  nand nand_4 (nand_4_out, ~A, ~C, ~E, F);  // NAND_Gate
  nand nand_5 (nand_5_out, ~A, ~C, ~D, E);  // NAND_Gate
  nand nand_6 (nand_6_out, ~B, ~C, D, ~E);  // NAND_Gate
  nand nand_7 (nand_7_out, ~B, C, E, ~F);  // NAND_Gate
  nand nand_8 (nand_8_out, B, C, D, ~F);  // NAND_Gate
  nand nand_9 (nand_9_out, C, D);
  nand nand_10 (nand_10_out, ~B, D, ~F);  // NAND_Gate
  nand nand_11 (nand_11_out, ~B, D, ~E);  // NAND_Gate
  nand nand_12 (nand_12_out, A, ~E, F);  // NAND_Gate
  nand nand_13 (nand_13_out, D, ~E, ~F);  // NAND_Gate
  nand nand_14 (nand_14_out, ~C, ~D, E, ~F);  // NAND_Gate
  nand nand_15 (nand_15_out, B, D, E, F);
  nand nand_16 (nand_16_out, ~A, ~B, ~D, E, F);  // NAND_Gate
  nand nand_17 (nand_17_out, B, ~C, ~D, ~E, F);  // NAND_Gate
  nor nor_1 (nor_1_out, B, E);
  nand nand_18 (nand_18_out, E, F);
  nand nand_19 (nand_19_out, B, ~F);  // NAND_Gate
  nand nand_20 (nand_20_out, A, F);
  nand nand_21 (nand_21_out, ~B, ~C, D);  // NAND_Gate
  nand nand_22 (nand_22_out, D, ~E, F);  // NAND_Gate
  nand nand_23 (nand_23_out, C, ~D, E);  // NAND_Gate
  nand nand_24 (nand_24_out, B, D, F);
  nand nand_25 (nand_25_out, ~B, ~C, E, F);  // NAND_Gate
  nand nand_26 (nand_26_out, B, ~C, ~D, ~E);  // NAND_Gate
  nand nand_27 (nand_27_out, B, C, D, ~E);  // NAND_Gate
  nor nor_2 (nor_2_out, E, F);
  nor nor_3 (nor_3_out, B, C);
  nor nor_4 (nor_4_out, C, E);
  nand nand_28 (nand_28_out, ~D, F);  // NAND_Gate
  nand nand_29 (nand_29_out, ~B, F);  // NAND_Gate
  nand nand_30 (nand_30_out, B, E);
  nand nand_31 (nand_31_out, ~B, D);  // NAND_Gate
  nand nand_32 (nand_32_out, B, ~E);  // NAND_Gate
  nand nand_33 (nand_33_out, ~B, C, ~F);  // NAND_Gate
  nand nand_34 (nand_34_out, ~B, C, E);  // NAND_Gate
  nand nand_35 (nand_35_out, A, E, F);
  nand nand_36 (nand_36_out, A, E);
  nor nor_5 (nor_5_out, A, B, C);
  nand nand_37 (nand_37_out, ~B, ~D, F);  // NAND_Gate
  nand nand_38 (nand_38_out, ~C, ~D, F);  // NAND_Gate
  nand nand_39 (nand_39_out, ~C, ~E, F);  // NAND_Gate
  nand nand_40 (nand_40_out, ~D, ~E, F);  // NAND_Gate
  nor nor_6 (nor_6_out, A, B, E, F);
  nand nand_41 (nand_41_out, C, D, E, F);
  nand nand_42 (nand_42_out, B, C, ~D, E, ~F);  // NAND_Gate
  nand nand_43 (nand_43_out, D, E);
  nand nand_44 (nand_44_out, D, F);
  nor nor_7 (nor_7_out, A, B, C);
  nor nor_8 (nor_8_out, A, B, D, E);
  nand nand_45 (nand_45_out, nand_1_out, nand_2_out, nand_3_out, nand_4_out, nand_5_out, nand_6_out, nand_7_out, nand_8_out);
  nand nand_46 (nand_46_out, nand_9_out, nand_10_out, nand_11_out, nand_12_out, nand_13_out, nand_14_out, nand_15_out, nand_16_out, nand_17_out);
  nand nand_47 (nand_47_out, C, D, ~nor_1_out, nand_18_out, nand_19_out);  // NAND_Gate
  nand nand_48 (nand_48_out, nand_20_out, nand_21_out, nand_22_out, nand_23_out, nand_24_out, nand_25_out, nand_26_out, nand_27_out);
  nand nand_49 (nand_49_out, ~nor_2_out, ~nor_3_out, ~nor_4_out, nand_28_out, nand_29_out, nand_30_out);  // NAND_Gate
  nand nand_50 (nand_50_out, nand_31_out, nand_32_out, nand_33_out, nand_34_out, nand_35_out);
  nand nand_51 (nand_51_out, nand_36_out, ~nor_5_out, nand_37_out, nand_38_out, nand_40_out, ~nor_6_out, nand_41_out, nand_42_out);  // NAND_Gate
  nand nand_52 (nand_52_out, ~C, nand_43_out, nand_44_out);  // NAND_Gate
  nor nor_9 (nor_9_out, nor_7_out, nor_8_out);
  nor nor_10 (nor_10_out, ~nand_45_out, ~1'b1);  // NOR_Gate
  nor nor_11 (nor_11_out, nand_45_out, ~1'b1);  // NOR_Gate
  nor nor_12 (nor_12_out, ~nand_46_out, ~nand_47_out);  // NOR_Gate
  nor nor_13 (nor_13_out, nand_46_out, ~nand_47_out);  // NOR_Gate
  nor nor_14 (nor_14_out, ~nand_48_out, ~nand_49_out);  // NOR_Gate
  nor nor_15 (nor_15_out, nand_48_out, ~nand_49_out);  // NOR_Gate
  nor nor_16 (nor_16_out, ~nand_50_out, ~nand_51_out);  // NOR_Gate
  nor nor_17 (nor_17_out, nand_50_out, ~nand_51_out);  // NOR_Gate
  nor nor_18 (nor_18_out, ~nand_52_out, nor_9_out);  // NOR_Gate
  nor nor_19 (nor_19_out, nand_52_out, nor_9_out);
  LED led_1 (.in(nor_10_out));
  _7_Segment_Display u_7_segment_display_1 (.a(nor_13_out));  // open: g, f, b, e, d, c, dp
  _7_Segment_Display u_7_segment_display_2 (.a(nor_11_out));  // open: g, f, b, e, d, c, dp
  LED led_2 (.in(nor_14_out));
  LED led_3 (.in(nor_12_out));
  _7_Segment_Display u_7_segment_display_3 (.a(nor_15_out));  // open: g, f, b, e, d, c, dp
  LED led_4 (.in(nor_16_out));
  _7_Segment_Display u_7_segment_display_4 (.a(nor_17_out));  // open: g, f, b, e, d, c, dp
  LED led_5 (.in(nor_18_out));
  _7_Segment_Display u_7_segment_display_5 (.a(nor_19_out));  // open: g, f, b, e, d, c, dp

  // Notes on the sheet:
  //   Display [4]
  //   MORSE [3]
  //   Display [3]
  //   MORSE [2]
  //   Display [2]
  //   MORSE [0]
  //   MORSE [4]
  //   MORSE [1]
  //   Display [1]
  //   Display [0]
  //   Ponto
  //   Traço
endmodule
