// Logisim project NAND.circ as structural Verilog: 1 circuit, main circuit main
module main (
  input  A,
  input  B,
  input  C,
  input  D,
  output out_5,
  output out_6,
  output out_7,
  output out_8,
  output out_9
);

  wire nand_1_out, nand_2_out, nand_3_out, nand_4_out, nand_5_out, nand_6_out, nand_7_out, nand_8_out;

  nand nand_1 (nand_1_out, ~A, ~B, D);  // NAND_Gate
  nand nand_2 (nand_2_out, ~B, C);  // NAND_Gate
  nand nand_3 (nand_3_out, B, ~C);  // NAND_Gate
  nand nand_4 (nand_4_out, C, ~D);  // NAND_Gate
  nand nand_5 (nand_5_out, C, D);
  nand nand_6 (nand_6_out, A, ~D);  // NAND_Gate
  nand nand_7 (nand_7_out, B, D);
  nand nand_8 (nand_8_out, B, C);
  nand nand_9 (out_5, nand_1_out, nand_2_out, nand_3_out);
  nand nand_10 (out_6, nand_2_out, nand_3_out, nand_4_out);
  nand nand_11 (out_7, ~B, nand_5_out);  // NAND_Gate
  nand nand_12 (out_8, ~B, nand_6_out);  // NAND_Gate
  nand nand_13 (out_9, ~A, nand_7_out, nand_8_out);  // NAND_Gate
endmodule
