// Logisim project Normal.circ as structural Verilog: 1 circuit, main circuit main
module main (
  input  A,
  input  B,
  input  C,
  input  D,
  input  E,
  input  F
);

  wire and_1_out, and_2_out, and_3_out, and_4_out, and_5_out, and_6_out, and_7_out, and_8_out, and_9_out,
       and_10_out, and_11_out, and_12_out, and_13_out, and_14_out, and_15_out, and_16_out, and_17_out,
       and_18_out, and_19_out, and_20_out, and_21_out, and_22_out, and_23_out, and_24_out, and_25_out,
       and_26_out, and_27_out, and_28_out, and_29_out, and_30_out, and_31_out, and_32_out, and_33_out,
       and_34_out, and_35_out, and_36_out, and_37_out, and_38_out, and_39_out, and_40_out, and_41_out,
       and_42_out, and_43_out, and_44_out, and_45_out, and_46_out, and_47_out, and_48_out, and_49_out,
       and_50_out, and_51_out, and_52_out, and_53_out, and_54_out, and_55_out, and_56_out, and_57_out,
       and_58_out, and_59_out, and_60_out, and_61_out, and_62_out, or_1_out, or_2_out, or_3_out, or_4_out,
       or_5_out, or_6_out, or_7_out, or_8_out, or_9_out;

  and and_1 (and_1_out, C, D, E);
  and and_2 (and_2_out, B, ~D, F);  // AND_Gate
  and and_3 (and_3_out, A, ~E, ~F);  // AND_Gate
  and and_4 (and_4_out, ~A, ~C, ~E, F);  // AND_Gate
  and and_5 (and_5_out, ~A, ~C, ~D, E);  // AND_Gate
  and and_6 (and_6_out, ~B, ~C, D, ~E);  // AND_Gate
  and and_7 (and_7_out, ~B, C, E, ~F);  // AND_Gate
  and and_8 (and_8_out, B, C, D, ~F);  // AND_Gate
  and and_9 (and_9_out, C, D);
  and and_10 (and_10_out, ~B, D, ~F);  // AND_Gate
  and and_11 (and_11_out, ~B, D, ~E);  // AND_Gate
  and and_12 (and_12_out, A, ~E, F);  // AND_Gate
  and and_13 (and_13_out, D, ~E, ~F);  // AND_Gate
  and and_14 (and_14_out, ~C, ~D, E, ~F);  // AND_Gate
  and and_15 (and_15_out, B, D, E, F);
  and and_16 (and_16_out, ~A, ~B, ~D, E, F);  // AND_Gate
  and and_17 (and_17_out, B, ~C, ~D, ~E, F);  // AND_Gate
  and and_18 (and_18_out, ~B, ~E);  // AND_Gate
  and and_19 (and_19_out, E, F);
  and and_20 (and_20_out, B, ~F);  // AND_Gate
  and and_21 (and_21_out, A, F);
  and and_22 (and_22_out, ~B, ~C, D);  // AND_Gate
  and and_23 (and_23_out, D, ~E, F);  // AND_Gate
  and and_24 (and_24_out, C, ~D, E);  // AND_Gate
  and and_25 (and_25_out, B, D, F);
  and and_26 (and_26_out, ~B, ~C, E, F);  // AND_Gate
  and and_27 (and_27_out, B, ~C, ~D, ~E);  // AND_Gate
  and and_28 (and_28_out, B, C, D, ~E);  // AND_Gate
  and and_29 (and_29_out, ~E, ~F);  // AND_Gate
  and and_30 (and_30_out, ~B, ~C);  // AND_Gate
  and and_31 (and_31_out, ~C, ~E);  // AND_Gate
  and and_32 (and_32_out, ~D, F);  // AND_Gate
  and and_33 (and_33_out, ~B, F);  // AND_Gate
  and and_34 (and_34_out, B, C, E);
  and and_35 (and_35_out, ~B, D);  // AND_Gate
  and and_36 (and_36_out, B, ~E);  // AND_Gate
  and and_37 (and_37_out, ~B, C, ~F);  // AND_Gate
  and and_38 (and_38_out, ~B, C, E);  // AND_Gate
  and and_39 (and_39_out, A, E, F);
  and and_40 (and_40_out, A, E);
  and and_41 (and_41_out, ~A, ~B, ~C);  // AND_Gate
  and and_42 (and_42_out, ~B, ~D, F);  // AND_Gate
  and and_43 (and_43_out, ~C, ~D, F);  // AND_Gate
  and and_44 (and_44_out, ~C, ~E, F);  // AND_Gate
  and and_45 (and_45_out, ~D, ~E, F);  // AND_Gate
  and and_46 (and_46_out, ~A, ~B, ~E, ~F);  // AND_Gate
  and and_47 (and_47_out, C, D, E, F);
  and and_48 (and_48_out, B, C, ~D, E, ~F);  // AND_Gate
  and and_49 (and_49_out, D, E);
  and and_50 (and_50_out, D, F);
  and and_51 (and_51_out, ~A, ~B, ~C);  // AND_Gate
  and and_52 (and_52_out, ~A, ~B, ~D, ~E);  // AND_Gate
  or or_1 (or_1_out, and_1_out, and_2_out, and_3_out, and_4_out, and_5_out, and_6_out, and_7_out, and_8_out);
  or or_2 (or_2_out, and_9_out, and_10_out, and_11_out, and_12_out, and_13_out, and_14_out, and_15_out, and_16_out, and_17_out);
  or or_3 (or_3_out, ~C, ~D, and_18_out, and_19_out, and_20_out);  // OR_Gate
  or or_4 (or_4_out, and_21_out, and_22_out, and_23_out, and_24_out, and_25_out, and_26_out, and_27_out, and_28_out);
  or or_5 (or_5_out, and_29_out, and_30_out, and_31_out, and_32_out, and_33_out, and_34_out);
  or or_6 (or_6_out, and_35_out, and_36_out, and_37_out, and_38_out, and_39_out);
  or or_7 (or_7_out, and_40_out, and_41_out, and_42_out, and_43_out, and_44_out, and_45_out, and_46_out, and_47_out, and_48_out);
  or or_8 (or_8_out, C, and_49_out, and_50_out);
  or or_9 (or_9_out, and_51_out, and_52_out);
  and and_53 (and_53_out, or_1_out, 1'b1);
  and and_54 (and_54_out, ~or_1_out, 1'b1);  // AND_Gate
  and and_55 (and_55_out, or_2_out, or_3_out);
  and and_56 (and_56_out, ~or_2_out, or_3_out);  // AND_Gate
  and and_57 (and_57_out, or_4_out, or_5_out);
  and and_58 (and_58_out, ~or_4_out, or_5_out);  // AND_Gate
  and and_59 (and_59_out, or_6_out, or_7_out);
  and and_60 (and_60_out, ~or_6_out, or_7_out);  // AND_Gate
  and and_61 (and_61_out, or_8_out, or_9_out);
  and and_62 (and_62_out, ~or_8_out, or_9_out);  // AND_Gate
  _7_Segment_Display u_7_segment_display_1 (.a(and_54_out));  // open: g, f, b, e, d, c, dp
  LED led_1 (.in(and_53_out));
  LED led_2 (.in(and_55_out));
  _7_Segment_Display u_7_segment_display_2 (.a(and_56_out));  // open: g, f, b, e, d, c, dp
  LED led_3 (.in(and_57_out));
  _7_Segment_Display u_7_segment_display_3 (.a(and_58_out));  // open: g, f, b, e, d, c, dp
  LED led_4 (.in(and_59_out));
  _7_Segment_Display u_7_segment_display_4 (.a(and_60_out));  // open: g, f, b, e, d, c, dp
  LED led_5 (.in(and_61_out));
  _7_Segment_Display u_7_segment_display_5 (.a(and_62_out));  // open: g, f, b, e, d, c, dp

  // Notes on the sheet:
  //   Display [4]
  //   MORSE [3]
  //   Display [3]
  //   MORSE [2]
  //   Display [2]
  //   MORSE [0]
  //   MORSE [4]
  //   MORSE [1]
  //   Display [1]
  //   Display [0]
  //   Ponto
  //   Traço
endmodule
